// Logisim project ALU_Group11.circ as structural Verilog: 12 circuits, main circuit main
module main (
  output halt,
  output [8:0] counter,
  output [3:0] op,
  output [11:0] a,
  output [11:0] b,
  output [11:0] result,
  output err_oracle,
  output error,
  output ok,
  output start_delimiter
);

  wire and_1_out, and_2_out, clock_1_out, comparator_1_eq, comparator_2_eq;

  Clock clock_1 (.out(clock_1_out));
  Counter #(.width(9), .max('h1ff), .trigger("falling")) counter_1 (
    .Q(counter), .carry(halt), .clk(clock_1_out));  // open: load, D, count, clr
  RAM #(.addrWidth(12), .dataWidth(4), .bus("separate")) ram_1 (
    .addr({counter, 3'b000}), .data(op), .ld(1'b1));  // open: din, str, sel, clk, clr
  RAM #(.addrWidth(12), .dataWidth(12), .bus("separate")) ram_2 (
    .addr({counter, 3'b001}), .data(a), .ld(1'b1));  // open: din, str, sel, clk, clr
  RAM #(.addrWidth(12), .dataWidth(12), .bus("separate")) ram_3 (
    .addr({counter, 3'b010}), .data(a), .ld(1'b1));  // open: din, str, sel, clk, clr
  RAM #(.addrWidth(12), .dataWidth(12), .bus("separate")) ram_4 (
    .addr({counter, 3'b011}), .data(a), .ld(1'b1));  // open: din, str, sel, clk, clr
  RAM #(.addrWidth(12), .dataWidth(1), .bus("separate")) ram_5 (
    .addr({counter, 3'b100}), .data(err_oracle), .ld(1'b1));  // open: din, str, sel, clk, clr
  RAM #(.addrWidth(12), .dataWidth(1), .bus("separate")) ram_6 (
    .addr({counter, 3'b101}), .data(start_delimiter), .ld(1'b1));  // open: din, str, sel, clk, clr
  // _12_bit_ALU 12_bit_alu_1: pin names not known; wires that end beside it: a, op, op, result, error
  Comparator #(.width(1), .mode("unsigned")) comparator_1 (
    .a(error), .b(err_oracle), .eq(comparator_1_eq));  // open: gt, lt
  Comparator #(.width(12)) comparator_2 (.a(result), .b(a), .eq(comparator_2_eq));  // open: gt, lt
  and and_1 (and_1_out, comparator_1_eq, error);
  and and_2 (and_2_out, comparator_2_eq, comparator_1_eq, ~error);  // AND_Gate
  or or_1 (ok, and_1_out, and_2_out);
  _12_bit_ALU u_12_bit_alu_2 ();  // open: ALU_code, a, b, overflow, result

  assign b = a;

  // Notes on the sheet:
  //   You must complete the circuit '12-bit ALU' instead.
  //   DO NOT EDIT THIS CIRCUIT!
endmodule

module _12_bit_ALU (
  input  [3:0] ALU_code,
  input  [11:0] a,
  input  [11:0] b,
  output [11:0] result,
  output overflow
);

  wire and_1_out, comparator_1_eq, comparator_2_eq, comparator_3_eq, opcode_decoder_1_b, opcode_decoder_1_c,
       or_1_out;
  wire [3:0] bitselector_1_out;
  wire [11:0] and_2_out, bit_extender_1_out, multiplexer_1_out, multiplexer_2_out,
       n3_12_bit_twos_complement_cla_1_sum, n0101_lt_1_lessout, n0110_gt_1_greaterout, n0111_eq_1_equealsout,
       n1000_neq_1_nequalsout, n1011_sll_1_out, n1100_srl_1_out, n1110_sra_1_out, not_1_out, not_2_sum,
       or_2_out, shifter_1_out;

  assign not_1_out = ~b;  // NOT_Gate not_1, 12 bits wide
  assign bit_extender_1_out = {{8{1'b0}}, ALU_code};  // Bit_Extender bit_extender_1
  Multiplexer #(.width(12)) multiplexer_1 (
    .in0(b), .in1(not_1_out), .out(multiplexer_1_out), .sel(opcode_decoder_1_b));  // open: en
  BitSelector #(.width(12), .group(4)) bitselector_1 (.in(a), .out(bitselector_1_out), .sel(2'b00));
  Comparator #(.width(12)) comparator_1 (.a(a), .b({12{1'b0}}), .eq(comparator_1_eq));  // open: gt, lt
  Comparator #(.width(12)) comparator_2 (.a(bit_extender_1_out), .b(12'hb), .eq(comparator_2_eq));  // open: gt, lt
  Comparator #(.width(12)) comparator_3 (.a(bit_extender_1_out), .b(12'hd), .eq(comparator_3_eq));  // open: gt, lt
  or or_1 (or_1_out, comparator_2_eq, comparator_3_eq);
  opcode_decoder opcode_decoder_1 (.in_1(ALU_code), .B(opcode_decoder_1_b), .C(opcode_decoder_1_c));
  and and_1 (and_1_out, comparator_1_eq, or_1_out);
  assign or_2_out = a | multiplexer_1_out;  // OR_Gate or_2, 12 bits wide
  assign and_2_out = a & multiplexer_1_out;  // AND_Gate and_2, 12 bits wide
  _3_12_bit_twos_complement_cla u_3_12_bit_twos_complement_cla_1 (
    .aIn(a), .bIn(multiplexer_1_out), .carryIn(opcode_decoder_1_c), .Sum(n3_12_bit_twos_complement_cla_1_sum));  // open: Overflow
  _0101_lt u_0101_lt_1 (.aIn(a), .bIn(multiplexer_1_out), .lessOut(n0101_lt_1_lessout));
  _0110_gt u_0110_gt_1 (.aIn(a), .bIn(multiplexer_1_out), .greaterOut(n0110_gt_1_greaterout));
  _0111_eq u_0111_eq_1 (.aIn(a), .bIn(multiplexer_1_out), .equealsOut(n0111_eq_1_equealsout));
  _1000_neq u_1000_neq_1 (.aIn(a), .bIn(multiplexer_1_out), .nequalsOut(n1000_neq_1_nequalsout));
  _3_12_bit_twos_complement_cla not_2 (
    .aIn(multiplexer_1_out), .bIn({12{1'b0}}), .carryIn(opcode_decoder_1_c), .Sum(not_2_sum));  // open: Overflow
  Shifter #(.width(12)) shifter_1 (.in(multiplexer_1_out), .\dist (bitselector_1_out), .out(shifter_1_out));
  _1011_sll u_1011_sll_1 (.in_1(multiplexer_1_out), .out(n1011_sll_1_out));
  _1100_srl u_1100_srl_1 (.in_1(a), .out(n1100_srl_1_out));
  _1110_sra u_1110_sra_1 (.in(a), .out(n1110_sra_1_out));
  overflow_detection_unit overflow_detection_unit_1 (
    .opcodeIn(ALU_code), .a(a), .b(b), .out(result), .overflowOut(overflow));
  Multiplexer #(.width(12), .enable("false")) multiplexer_2 (
    .in0(shifter_1_out), .in1(n1011_sll_1_out), .out(multiplexer_2_out), .sel(and_1_out));
  Multiplexer #(.select(4), .width(12)) multiplexer_3 (
    .in0({12{1'b0}}), .in1(or_2_out), .in2(and_2_out), .in3(n3_12_bit_twos_complement_cla_1_sum),
    .in4(n3_12_bit_twos_complement_cla_1_sum), .in5(n0101_lt_1_lessout), .in6(n0110_gt_1_greaterout),
    .in7(n0111_eq_1_equealsout), .in8(n1000_neq_1_nequalsout), .in9(not_2_sum), .in10(not_2_sum),
    .in11(multiplexer_2_out), .in12(n1100_srl_1_out), .in13(multiplexer_2_out), .in14(n1110_sra_1_out),
    .in15(a), .out(result), .sel(ALU_code));  // open: en

  // Notes on the sheet:
  //   This circuit is used as a block in the main circuit, and its layout must remain unchanged. The circuit called "main" should be the main circuit of this file.
  //   Do not change the circuit appearance.
  //   DO NOT CHANGE THE INPUTS AND OUTPUTS OF THIS CIRCUIT!
  //   Do not add/remove inputs or outputs. Do not even change their location or orientation.
endmodule

// decoder
module opcode_decoder (
  input  [3:0] in_1,
  output B,
  output C
);

  wire and_1_out, and_2_out, and_3_out, and_4_out, and_5_out, not_1_out, not_2_out, not_3_out, not_4_out,
       not_5_out, not_6_out, not_7_out, not_8_out, not_9_out, not_10_out, not_11_out, not_12_out;

  not not_1 (not_1_out, in_1[2]);
  not not_2 (not_2_out, in_1[1]);
  not not_3 (not_3_out, in_1[2]);
  not not_4 (not_4_out, in_1[0]);
  not not_5 (not_5_out, in_1[3]);
  not not_6 (not_6_out, in_1[1]);
  not not_7 (not_7_out, in_1[0]);
  not not_8 (not_8_out, in_1[3]);
  not not_9 (not_9_out, in_1[1]);
  not not_10 (not_10_out, in_1[0]);
  not not_11 (not_11_out, in_1[2]);
  not not_12 (not_12_out, in_1[0]);
  and and_1 (and_1_out, in_1[3], not_1_out, not_2_out, in_1[0]);
  and and_2 (and_2_out, in_1[3], not_3_out, in_1[1], not_4_out);
  or or_1 (B, and_1_out, and_2_out, and_3_out);
  and and_3 (and_3_out, not_5_out, in_1[2], not_6_out, not_7_out);
  and and_4 (and_4_out, not_8_out, in_1[2], not_9_out, not_10_out);
  or or_2 (C, and_4_out, and_5_out);
  and and_5 (and_5_out, in_1[3], not_11_out, in_1[1], not_12_out);
endmodule

// SLL
module _1011_sll (
  input  [11:0] in_1,
  output [11:0] out
);


  assign out = {in_1[10:0], 1'b0};
endmodule

// SRL
module _1100_srl (
  input  [11:0] in_1,
  output [11:0] out
);


  assign out = {1'b0, in_1[11:1]};
endmodule

// ==
module _0111_eq (
  input  [11:0] aIn,
  input  [11:0] bIn,
  output [11:0] equealsOut
);

  wire and_1_out;
  wire [11:0] xnor_1_out;

  assign xnor_1_out = ~(aIn ^ bIn);  // XNOR_Gate xnor_1, 12 bits wide
  and and_1 (and_1_out, xnor_1_out[0], xnor_1_out[1], xnor_1_out[2], xnor_1_out[3], xnor_1_out[4], xnor_1_out[5], xnor_1_out[6], xnor_1_out[7], xnor_1_out[8], xnor_1_out[9], xnor_1_out[10], xnor_1_out[11]);
  assign equealsOut = {{11{1'b0}}, and_1_out};  // Bit_Extender bit_extender_1
endmodule

// <
module _0101_lt (
  input  [11:0] aIn,
  input  [11:0] bIn,
  output [11:0] lessOut
);

  wire and_1_out, and_2_out, not_2_out, or_1_out, S_out;
  wire [11:0] n3_12_bit_twos_complement_cla_1_sum, not_1_out;

  xnor S (S_out, aIn[11], bIn[11]);
  assign not_1_out = ~bIn;  // NOT_Gate not_1, 12 bits wide
  _3_12_bit_twos_complement_cla u_3_12_bit_twos_complement_cla_1 (
    .aIn(aIn), .bIn(not_1_out), .carryIn(1'b1), .Sum(n3_12_bit_twos_complement_cla_1_sum));  // open: Overflow
  not not_2 (not_2_out, S_out);
  and and_1 (and_1_out, S_out, n3_12_bit_twos_complement_cla_1_sum[11]);
  or or_1 (or_1_out, and_1_out, and_2_out);
  and and_2 (and_2_out, not_2_out, aIn[11]);
  assign lessOut = {{11{1'b0}}, or_1_out};  // Bit_Extender bit_extender_1
endmodule

// >
module _0110_gt (
  input  [11:0] aIn,
  input  [11:0] bIn,
  output [11:0] greaterOut
);

  wire not_1_out, xor_1_out;
  wire [11:0] n0101_lt_1_lessout, n0111_eq_1_equealsout;

  _0101_lt u_0101_lt_1 (.aIn(aIn), .bIn(bIn), .lessOut(n0101_lt_1_lessout));
  _0111_eq u_0111_eq_1 (.aIn(aIn), .bIn(bIn), .equealsOut(n0111_eq_1_equealsout));
  not not_1 (not_1_out, n0101_lt_1_lessout[0]);
  xor xor_1 (xor_1_out, not_1_out, n0111_eq_1_equealsout[0]);
  assign greaterOut = {{11{1'b0}}, xor_1_out};  // Bit_Extender bit_extender_1
endmodule

// !=
module _1000_neq (
  input  [11:0] aIn,
  input  [11:0] bIn,
  output [11:0] nequalsOut
);

  wire not_1_out;
  wire [11:0] n0111_eq_1_equealsout;

  _0111_eq u_0111_eq_1 (.aIn(aIn), .bIn(bIn), .equealsOut(n0111_eq_1_equealsout));
  not not_1 (not_1_out, n0111_eq_1_equealsout[0]);
  assign nequalsOut = {{11{1'b0}}, not_1_out};  // Bit_Extender bit_extender_1
endmodule

// sra
module _1110_sra (
  input  [11:0] in,
  output [11:0] out
);


  assign out = {{2{in[11]}}, in[10:1]};
endmodule

module _0100_sub (
  input  [11:0] aIn,
  input  [11:0] bIn
);

  _3_12_bit_twos_complement_cla u_3_12_bit_twos_complement_cla_1 (
    .aIn(aIn), .bIn(bIn));  // open: carryIn, Sum, Overflow
endmodule

module overflow_detection_unit (
  input  [3:0] opcodeIn,
  input  [11:0] a,
  input  [11:0] b,
  input  [11:0] out,
  output overflowOut
);

  wire and_1_out, and_2_out, and_3_out, and_4_out, and_5_out, or_1_out, or_2_out, xnor_1_out, xor_1_out,
       xor_2_out;

  and and_1 (and_1_out, a[11], b[11], ~out[11]);  // AND_Gate
  and and_2 (and_2_out, ~a[11], ~b[11], out[11]);  // AND_Gate
  and and_3 (and_3_out, a[11], ~b[11], ~out[11]);  // AND_Gate
  and and_4 (and_4_out, ~a[11], b[11], out[11]);  // AND_Gate
  xnor xnor_1 (xnor_1_out, out[11], a[11]);
  and and_5 (and_5_out, ~out[11], ~a[11]);  // AND_Gate
  xor xor_1 (xor_1_out, b[11], out[11]);
  or or_1 (or_1_out, and_1_out, and_2_out);
  or or_2 (or_2_out, and_3_out, and_4_out);
  xor xor_2 (xor_2_out, xnor_1_out, and_5_out);
  Multiplexer #(.select(4)) multiplexer_1 (
    .in0(1'b0), .in1(1'b0), .in2(1'b0), .in3(or_1_out), .in4(or_2_out), .in5(1'b0), .in6(1'b0), .in7(1'b0),
    .in8(1'b0), .in9(1'b0), .in10(xor_2_out), .in11(1'b0), .in12(1'b0), .in13(xor_1_out), .in14(1'b0),
    .in15(1'b0), .out(overflowOut), .sel(opcodeIn));  // open: en
endmodule
