// Logisim project Adders.circ as structural Verilog
module _1_1_bit_sum (
  input  carryIn,
  input  aIn,
  input  bIn,
  output sumOut
);

  wire and_1_out, and_2_out, and_3_out, and_4_out, not_1_out, not_2_out, not_3_out, not_4_out, not_5_out,
       not_6_out;

  not not_1 (not_1_out, bIn);
  not not_2 (not_2_out, carryIn);
  not not_3 (not_3_out, aIn);
  not not_4 (not_4_out, carryIn);
  not not_5 (not_5_out, aIn);
  not not_6 (not_6_out, bIn);
  and and_1 (and_1_out, aIn, not_1_out, not_2_out);
  and and_2 (and_2_out, not_3_out, bIn, not_4_out);
  and and_3 (and_3_out, not_5_out, not_6_out, carryIn);
  and and_4 (and_4_out, aIn, bIn, carryIn);
  or or_1 (sumOut, and_1_out, and_2_out, and_3_out, and_4_out);
endmodule

module _1_1_bit_carry (
  input  carryIn,
  input  aIn,
  input  bIn,
  output carryOut
);

  wire and_1_out, and_2_out, and_3_out;

  and and_1 (and_1_out, aIn, carryIn);
  and and_2 (and_2_out, bIn, carryIn);
  and and_3 (and_3_out, aIn, bIn);
  or or_1 (carryOut, and_1_out, and_2_out, and_3_out);
endmodule

module _1_1_bit_adder (
  input  carryIn,
  input  aIn,
  input  bIn,
  output sumOut,
  output carryOut
);

  _1_1_bit_sum u_1_1_bit_sum_1 (.carryIn(carryIn), .aIn(aIn), .bIn(bIn), .sumOut(sumOut));
  _1_1_bit_carry u_1_1_bit_carry_1 (.carryIn(carryIn), .aIn(aIn), .bIn(bIn), .carryOut(carryOut));
endmodule

module _2_overflow_detection (
  input  [11:0] msbA,
  input  [11:0] msbB,
  input  [11:0] msbOut,
  output overflowOut
);

  wire and_1_out, and_2_out, not_1_out, not_2_out, not_3_out;

  not not_1 (not_1_out, msbOut[11]);
  not not_2 (not_2_out, msbA[11]);
  not not_3 (not_3_out, msbB[11]);
  and and_1 (and_1_out, msbA[11], msbB[11], not_1_out);
  and and_2 (and_2_out, not_2_out, not_3_out, msbOut[11]);
  or or_1 (overflowOut, and_1_out, and_2_out);
endmodule

module _2_12_bit_twos_complement_ripple_carry_adder (
  input  carryIn,
  input  [11:0] aIn,
  input  [11:0] bIn,
  output [11:0] additionOut,
  output overflowOut
);

  wire n1_1_bit_adder_1_carryout, n1_1_bit_adder_2_carryout, n1_1_bit_adder_3_carryout,
       n1_1_bit_adder_4_carryout, n1_1_bit_adder_5_carryout, n1_1_bit_adder_6_carryout,
       n1_1_bit_adder_7_carryout, n1_1_bit_adder_8_carryout, n1_1_bit_adder_9_carryout,
       n1_1_bit_adder_10_carryout, n1_1_bit_adder_11_carryout;

  _1_1_bit_adder u_1_1_bit_adder_1 (
    .carryIn(carryIn), .aIn(aIn[0]), .bIn(bIn[0]), .sumOut(additionOut[0]),
    .carryOut(n1_1_bit_adder_1_carryout));
  _1_1_bit_adder u_1_1_bit_adder_2 (
    .carryIn(n1_1_bit_adder_1_carryout), .aIn(aIn[1]), .bIn(bIn[1]), .sumOut(additionOut[1]),
    .carryOut(n1_1_bit_adder_2_carryout));
  _1_1_bit_adder u_1_1_bit_adder_3 (
    .carryIn(n1_1_bit_adder_2_carryout), .aIn(aIn[2]), .bIn(bIn[2]), .sumOut(additionOut[2]),
    .carryOut(n1_1_bit_adder_3_carryout));
  _1_1_bit_adder u_1_1_bit_adder_4 (
    .carryIn(n1_1_bit_adder_3_carryout), .aIn(aIn[3]), .bIn(bIn[3]), .sumOut(additionOut[3]),
    .carryOut(n1_1_bit_adder_4_carryout));
  _1_1_bit_adder u_1_1_bit_adder_5 (
    .carryIn(n1_1_bit_adder_4_carryout), .aIn(aIn[4]), .bIn(bIn[4]), .sumOut(additionOut[4]),
    .carryOut(n1_1_bit_adder_5_carryout));
  _1_1_bit_adder u_1_1_bit_adder_6 (
    .carryIn(n1_1_bit_adder_5_carryout), .aIn(aIn[5]), .bIn(bIn[5]), .sumOut(additionOut[5]),
    .carryOut(n1_1_bit_adder_6_carryout));
  _1_1_bit_adder u_1_1_bit_adder_7 (
    .carryIn(n1_1_bit_adder_6_carryout), .aIn(aIn[6]), .bIn(bIn[6]), .sumOut(additionOut[6]),
    .carryOut(n1_1_bit_adder_7_carryout));
  _1_1_bit_adder u_1_1_bit_adder_8 (
    .carryIn(n1_1_bit_adder_7_carryout), .aIn(aIn[7]), .bIn(bIn[7]), .sumOut(additionOut[7]),
    .carryOut(n1_1_bit_adder_8_carryout));
  _1_1_bit_adder u_1_1_bit_adder_9 (
    .carryIn(n1_1_bit_adder_8_carryout), .aIn(aIn[8]), .bIn(bIn[8]), .sumOut(additionOut[8]),
    .carryOut(n1_1_bit_adder_9_carryout));
  _1_1_bit_adder u_1_1_bit_adder_10 (
    .carryIn(n1_1_bit_adder_9_carryout), .aIn(aIn[9]), .bIn(bIn[9]), .sumOut(additionOut[9]),
    .carryOut(n1_1_bit_adder_10_carryout));
  _1_1_bit_adder u_1_1_bit_adder_11 (
    .carryIn(n1_1_bit_adder_10_carryout), .aIn(aIn[10]), .bIn(bIn[10]), .sumOut(additionOut[10]),
    .carryOut(n1_1_bit_adder_11_carryout));
  _1_1_bit_adder u_1_1_bit_adder_12 (
    .carryIn(n1_1_bit_adder_11_carryout), .aIn(aIn[11]), .bIn(bIn[11]), .sumOut(additionOut[11]));  // open: carryOut
  _2_overflow_detection u_2_overflow_detection_1 (
    .msbA(aIn), .msbB(bIn), .msbOut(additionOut), .overflowOut(overflowOut));
endmodule

module _3_4_bit_carry_lookahead_adder (
  input  carryIn,
  input  [3:0] aIn,
  input  [3:0] bIn,
  output [3:0] additionOut,
  output superPropagateOut,
  output superGenerateOut
);

  wire and_1_out, and_2_out, and_3_out, and_4_out, and_5_out, and_6_out, and_7_out, and_8_out, and_9_out,
       c1_out, c2_out, c3_out, g0_out, g1_out, g2_out, g3_out, p0_out, p1_out, p2_out, p3_out;

  and g3 (g3_out, aIn[3], bIn[3]);
  and g2 (g2_out, aIn[2], bIn[2]);
  and g1 (g1_out, aIn[1], bIn[1]);
  and g0 (g0_out, aIn[0], bIn[0]);
  or p3 (p3_out, aIn[3], bIn[3]);
  or p2 (p2_out, aIn[2], bIn[2]);
  or p1 (p1_out, aIn[1], bIn[1]);
  or p0 (p0_out, aIn[0], bIn[0]);
  and and_1 (and_1_out, p0_out, carryIn);
  or c1 (c1_out, and_1_out, g0_out);
  and and_2 (and_2_out, p0_out, p1_out, carryIn);
  or c2 (c2_out, and_2_out, and_3_out, g1_out);
  and and_3 (and_3_out, p1_out, g0_out);
  and and_4 (and_4_out, p0_out, p1_out, p2_out, carryIn);
  and and_5 (and_5_out, p1_out, p2_out, g0_out);
  and and_6 (and_6_out, p2_out, g1_out);
  and and_7 (and_7_out, p1_out, p2_out, p3_out, g0_out);
  and and_8 (and_8_out, p2_out, p3_out, g1_out);
  and and_9 (and_9_out, p3_out, g2_out);
  or c3 (c3_out, and_4_out, and_5_out, and_6_out, g2_out);
  and P0_2 (superPropagateOut, p0_out, p1_out, p2_out, p3_out);
  or G0_2 (superGenerateOut, and_7_out, and_8_out, and_9_out, g3_out);
  _1_1_bit_adder u_1_1_bit_adder_1 (
    .carryIn(carryIn), .aIn(aIn[0]), .bIn(bIn[0]), .sumOut(additionOut[0]));  // open: carryOut
  _1_1_bit_adder u_1_1_bit_adder_2 (
    .carryIn(c1_out), .aIn(aIn[1]), .bIn(bIn[1]), .sumOut(additionOut[1]));  // open: carryOut
  _1_1_bit_adder u_1_1_bit_adder_3 (
    .carryIn(c2_out), .aIn(aIn[2]), .bIn(bIn[2]), .sumOut(additionOut[2]));  // open: carryOut
  _1_1_bit_adder u_1_1_bit_adder_4 (
    .carryIn(c3_out), .aIn(aIn[3]), .bIn(bIn[3]), .sumOut(additionOut[3]));  // open: carryOut
endmodule

module _3_carry_lookahead_unit (
  input  c0,
  input  G0,
  input  P0,
  input  G1,
  input  P1,
  input  [3:0] sum0,
  input  [3:0] sum1,
  input  [3:0] sum2,
  output C1,
  output C2,
  output [11:0] Sum
);

  wire and_1_out, and_2_out, and_3_out;

  and and_1 (and_1_out, c0, P0);
  or or_1 (C1, and_1_out, G0);
  and and_2 (and_2_out, c0, P0, P1);
  or or_2 (C2, and_2_out, and_3_out, G1);
  and and_3 (and_3_out, P1, G0);

  assign Sum = {sum2, sum1, sum0};
endmodule

module _3_12_bit_twos_complement_cla (
  input  [11:0] aIn,
  input  [11:0] bIn,
  input  carryIn,
  output [11:0] Sum,
  output Overflow
);

  wire n3_4_bit_carry_lookahead_adder_1_supergenerateout, n3_4_bit_carry_lookahead_adder_1_superpropagateout,
       n3_4_bit_carry_lookahead_adder_2_supergenerateout, n3_4_bit_carry_lookahead_adder_2_superpropagateout,
       n3_carry_lookahead_unit_1_c1, n3_carry_lookahead_unit_1_c2;
  wire [3:0] n3_4_bit_carry_lookahead_adder_1_additionout, n3_4_bit_carry_lookahead_adder_2_additionout,
       n3_4_bit_carry_lookahead_adder_3_additionout;

  _3_4_bit_carry_lookahead_adder u_3_4_bit_carry_lookahead_adder_1 (
    .carryIn(carryIn), .aIn(aIn[3:0]), .bIn(bIn[3:0]),
    .additionOut(n3_4_bit_carry_lookahead_adder_1_additionout),
    .superPropagateOut(n3_4_bit_carry_lookahead_adder_1_superpropagateout),
    .superGenerateOut(n3_4_bit_carry_lookahead_adder_1_supergenerateout));
  _3_4_bit_carry_lookahead_adder u_3_4_bit_carry_lookahead_adder_2 (
    .carryIn(n3_carry_lookahead_unit_1_c1), .aIn(aIn[7:4]), .bIn(bIn[7:4]),
    .additionOut(n3_4_bit_carry_lookahead_adder_2_additionout),
    .superPropagateOut(n3_4_bit_carry_lookahead_adder_2_superpropagateout),
    .superGenerateOut(n3_4_bit_carry_lookahead_adder_2_supergenerateout));
  _3_4_bit_carry_lookahead_adder u_3_4_bit_carry_lookahead_adder_3 (
    .carryIn(n3_carry_lookahead_unit_1_c2), .aIn(aIn[11:8]), .bIn(bIn[11:8]),
    .additionOut(n3_4_bit_carry_lookahead_adder_3_additionout));  // open: superPropagateOut, superGenerateOut
  _3_carry_lookahead_unit u_3_carry_lookahead_unit_1 (
    .c0(carryIn), .G0(n3_4_bit_carry_lookahead_adder_1_supergenerateout),
    .P0(n3_4_bit_carry_lookahead_adder_1_superpropagateout),
    .G1(n3_4_bit_carry_lookahead_adder_2_supergenerateout),
    .P1(n3_4_bit_carry_lookahead_adder_2_superpropagateout),
    .sum0(n3_4_bit_carry_lookahead_adder_1_additionout), .sum1(n3_4_bit_carry_lookahead_adder_2_additionout),
    .sum2(n3_4_bit_carry_lookahead_adder_3_additionout), .C1(n3_carry_lookahead_unit_1_c1),
    .C2(n3_carry_lookahead_unit_1_c2), .Sum(Sum));
  _2_overflow_detection u_2_overflow_detection_1 (.msbA(aIn), .msbB(bIn), .msbOut(Sum), .overflowOut(Overflow));
endmodule
