// Logisim project SD_Group11.circ as structural Verilog: 8 circuits, main circuit main
module main (
  output [11:0] pc,
  output [11:0] r0,
  output [11:0] r1,
  output [11:0] r2,
  output [11:0] r3,
  output [11:0] r4,
  output [11:0] r5,
  output [11:0] r6,
  output [11:0] r7,
  output halt
);

  wire and_1_out, bitselector_1_out, clock_1_out, control_1_alusrc, control_1_babs, control_1_brneqzero,
       control_1_jumpreg, control_1_loadupperimm, control_1_memread, control_1_memtoreg, control_1_memwrite,
       control_1_regwrite, instruction_splitter_1_except, n12_bit_alu_1_overflow, or_1_out, or_2_out,
       reset_out;
  wire [2:0] instruction_splitter_1_rd, instruction_splitter_1_rs, instruction_splitter_1_rt;
  wire [3:0] instruction_splitter_1_aluopout, instruction_splitter_1_icode;
  wire [11:0] instruction_splitter_1_addr, instruction_splitter_1_imm, multiplexer_1_out, multiplexer_2_out,
       multiplexer_3_out, multiplexer_4_out, multiplexer_5_out, multiplexer_6_out, n2_register_file_1_rsout,
       n2_register_file_1_rtout, n3_12_bit_twos_complement_cla_1_sum, n3_12_bit_twos_complement_cla_2_sum,
       n12_bit_alu_1_result, ram_2_data;
  wire [12:0] ram_1_data;

  Halt halt_1 (.instruction(ram_1_data), .clock(clock_1_out), .reset(reset_out), .halt(halt));
  Clock clock_1 (.out(clock_1_out));
  Button reset (.out(reset_out));
  or or_1 (or_1_out, halt, or_2_out);
  Multiplexer #(.width(12), .enable("false")) multiplexer_1 (
    .in0(multiplexer_2_out), .in1(multiplexer_6_out), .out(multiplexer_1_out), .sel(control_1_jumpreg));
  and and_1 (and_1_out, ~or_1_out, clock_1_out);  // AND_Gate
  Multiplexer #(.width(12), .enable("false")) multiplexer_2 (
    .in0(instruction_splitter_1_addr), .in1(multiplexer_3_out), .out(multiplexer_2_out),
    .sel(control_1_brneqzero));
  BitSelector #(.width(12)) bitselector_1 (.in(multiplexer_6_out), .out(bitselector_1_out), .sel(4'b0000));
  program_counter program_counter_1 (
    .C(and_1_out), .bv(multiplexer_1_out), .reset(reset_out), .babs(control_1_babs), .brel(1'b0), .O(pc));
  Multiplexer #(.width(12), .enable("false")) multiplexer_3 (
    .in0(n3_12_bit_twos_complement_cla_1_sum), .in1(n3_12_bit_twos_complement_cla_2_sum),
    .out(multiplexer_3_out), .sel(bitselector_1_out));
  _3_12_bit_twos_complement_cla u_3_12_bit_twos_complement_cla_1 (
    .aIn(pc), .bIn(12'h1), .carryIn(1'b0), .Sum(n3_12_bit_twos_complement_cla_1_sum));  // open: Overflow
  _3_12_bit_twos_complement_cla u_3_12_bit_twos_complement_cla_2 (
    .aIn(instruction_splitter_1_imm), .bIn(pc), .carryIn(1'b1), .Sum(n3_12_bit_twos_complement_cla_2_sum));  // open: Overflow
  RAM #(.addrWidth(12), .dataWidth(13)) ram_1 (
    .addr(pc), .data(ram_1_data), .clk(clock_1_out), .clr(reset_out));  // open: sel, ld
  control control_1 (
    .a(instruction_splitter_1_icode), .MemRead(control_1_memread), .MemWrite(control_1_memwrite),
    .MemToReg(control_1_memtoreg), .RegWrite(control_1_regwrite), .ALUsrc(control_1_alusrc),
    .jumpReg(control_1_jumpreg), .babs(control_1_babs), .loadUpperImm(control_1_loadupperimm),
    .brNeqZero(control_1_brneqzero));
  or or_2 (or_2_out, instruction_splitter_1_except, n12_bit_alu_1_overflow);
  instruction_splitter instruction_splitter_1 (
    .in_1(ram_1_data), .icode(instruction_splitter_1_icode), .rd(instruction_splitter_1_rd),
    .rs(instruction_splitter_1_rs), .rt(instruction_splitter_1_rt), .imm(instruction_splitter_1_imm),
    .ALUopout(instruction_splitter_1_aluopout), .addr(instruction_splitter_1_addr), .ins(pc),
    .except(instruction_splitter_1_except));
  _2_register_file u_2_register_file_1 (
    .clear(reset_out), .\input (multiplexer_6_out), .write(control_1_regwrite),
    .rd(instruction_splitter_1_rd), ._0(r0), ._1(r1), ._2(r2), ._3(r3), ._4(r4), ._5(r5), ._6(r6), ._7(r7),
    .rs(instruction_splitter_1_rs), .rt(instruction_splitter_1_rt), .rsOut(n2_register_file_1_rsout),
    .rtOut(n2_register_file_1_rtout), .clock(clock_1_out));
  Multiplexer #(.width(12), .enable("false")) multiplexer_4 (
    .in0(n2_register_file_1_rtout), .in1(instruction_splitter_1_imm), .out(multiplexer_4_out),
    .sel(control_1_alusrc));
  Multiplexer #(.width(12), .enable("false")) multiplexer_5 (
    .in0(n2_register_file_1_rsout), .in1(12'h6), .out(multiplexer_5_out), .sel(control_1_loadupperimm));
  _12_bit_ALU u_12_bit_alu_1 (
    .ALU_code(instruction_splitter_1_aluopout), .a(multiplexer_5_out), .b(multiplexer_4_out),
    .overflow(n12_bit_alu_1_overflow), .result(n12_bit_alu_1_result));
  RAM #(.addrWidth(12), .dataWidth(12), .bus("separate")) ram_2 (
    .addr(n12_bit_alu_1_result), .din(n2_register_file_1_rtout), .data(ram_2_data), .str(control_1_memwrite),
    .clk(clock_1_out), .ld(control_1_memread), .clr(reset_out));  // open: sel
  Multiplexer #(.width(12), .enable("false")) multiplexer_6 (
    .in0(n12_bit_alu_1_result), .in1(ram_2_data), .out(multiplexer_6_out), .sel(control_1_memtoreg));

  // Notes on the sheet:
  //   current instruction
  //   reset button
  //   clock signal
  //   DO NOT CHANGE THE INPUTS AND OUTPUTS OF THIS CIRCUIT! Do not add/remove inputs or outputs. Do not even change their location or orientation.
endmodule

module Halt (
  input  [12:0] instruction,
  input  clock,
  input  reset,
  output halt
);

  wire and_1_out, comparator_1_eq, comparator_2_gt, counter_1_carry, or_1_out, or_2_out;
  wire [11:0] counter_1_q;

  Comparator #(.width(13), .mode("unsigned")) comparator_1 (
    .a(instruction), .b({13{1'b0}}), .eq(comparator_1_eq));  // open: gt, lt
  Counter #(.width(12), .max('hfff), .trigger("falling")) counter_1 (
    .Q(counter_1_q), .carry(counter_1_carry), .clk(clock), .clr(reset));  // open: load, D, count
  or or_1 (or_1_out, comparator_1_eq, counter_1_carry);
  Comparator #(.width(12), .mode("unsigned")) comparator_2 (
    .a(counter_1_q), .b({12{1'b0}}), .gt(comparator_2_gt));  // open: eq, lt
  or or_2 (or_2_out, halt, and_1_out);
  and and_1 (and_1_out, or_1_out, comparator_2_gt);
  Register #(.width(1)) register_1 (.D(or_2_out), .Q(halt), .clk(clock), .clr(reset));  // open: en

  // Notes on the sheet:
  //   halt becomes and stays asserted if the instruction is 0000 (not in the first clock cycle) or the end of the counter is reached (2^12)
endmodule

module program_counter (
  input  C,
  input  [11:0] bv,
  input  reset,
  input  babs,
  input  brel,
  output [11:0] O
);

  wire or_1_out;
  wire [2:0] program_counter_encoder_1_out_4;
  wire [11:0] multiplexer_1_out, n3_12_bit_twos_complement_cla_1_sum, n3_12_bit_twos_complement_cla_2_sum;

  program_counter_encoder program_counter_encoder_1 (
    .reset(reset), .babs(babs), .brel(brel), .out_4(program_counter_encoder_1_out_4));
  or or_1 (or_1_out, C, reset);
  Multiplexer #(.select(3), .width(12), .enable("false")) multiplexer_1 (
    .in0(n3_12_bit_twos_complement_cla_1_sum), .in1(n3_12_bit_twos_complement_cla_2_sum), .in2(bv),
    .in3({12{1'b0}}), .in4(O), .out(multiplexer_1_out), .sel(program_counter_encoder_1_out_4));  // open: in5, in6, in7
  _1_12_bit_register u_1_12_bit_register_1 (.c(or_1_out), .D(multiplexer_1_out), .write(1'b1), .reset(1'b0), .Q(O));
  _3_12_bit_twos_complement_cla u_3_12_bit_twos_complement_cla_1 (
    .aIn(O), .bIn(12'h1), .carryIn(1'b0), .Sum(n3_12_bit_twos_complement_cla_1_sum));  // open: Overflow
  _3_12_bit_twos_complement_cla u_3_12_bit_twos_complement_cla_2 (
    .aIn(bv), .bIn(O), .carryIn(1'b0), .Sum(n3_12_bit_twos_complement_cla_2_sum));  // open: Overflow
endmodule

module program_counter_encoder (
  input  reset,
  input  babs,
  input  brel,
  output [2:0] out_4
);

  wire and_1_out, and_2_out, and_3_out, and_4_out, and_5_out, and_6_out, and_7_out, not_1_out, not_2_out,
       not_3_out, not_4_out, not_5_out, not_6_out, not_7_out, not_8_out;

  and and_1 (and_1_out, babs, brel);
  and and_2 (and_2_out, reset, brel);
  and and_3 (and_3_out, reset, babs);
  not not_1 (not_1_out, reset);
  not not_2 (not_2_out, brel);
  not not_3 (not_3_out, babs);
  not not_4 (not_4_out, brel);
  not not_5 (not_5_out, reset);
  not not_6 (not_6_out, babs);
  not not_7 (not_7_out, babs);
  not not_8 (not_8_out, brel);
  or or_1 (out_4[2], and_1_out, and_2_out, and_3_out);
  and and_4 (and_4_out, not_1_out, babs, not_2_out);
  and and_5 (and_5_out, reset, not_3_out, not_4_out);
  and and_6 (and_6_out, not_5_out, not_6_out, brel);
  and and_7 (and_7_out, reset, not_7_out, not_8_out);
  or or_2 (out_4[1], and_4_out, and_5_out);
  or or_3 (out_4[0], and_6_out, and_7_out);
endmodule

module instruction_splitter (
  input  [12:0] in_1,
  input  [11:0] ins,
  output [3:0] icode,
  output [2:0] rd,
  output [2:0] rs,
  output [2:0] rt,
  output [11:0] imm,
  output [11:0] addr,
  output [3:0] ALUopout,
  output except
);

  wire and_1_out, and_2_out, and_3_out, and_4_out, and_5_out, and_6_out, and_7_out, and_8_out, and_9_out,
       and_10_out, and_11_out, and_12_out, and_13_out, and_14_out, and_15_out, and_16_out, and_18_out,
       icodec_1_binary, icodec_1_brnz, icodec_1_j, icodec_1_jreg, icodec_1_li, icodec_1_meminstr,
       icodec_1_sw, icodec_1_unary, or_1_out, or_2_out, or_3_out, or_4_out, or_5_out, or_6_out, or_7_out;
  wire [2:0] multiplexer_3_out, multiplexer_8_out;
  wire [3:0] bit_extender_1_out, multiplexer_1_out, multiplexer_2_out, multiplexer_4_out, multiplexer_6_out,
       multiplexer_11_out;
  wire [11:0] bit_extender_2_out, bit_extender_3_out, bit_extender_4_out, multiplexer_9_out,
       multiplexer_10_out, multiplexer_14_out, n3_12_bit_twos_complement_cla_1_sum;

  and and_1 (and_1_out, ~in_1[0], in_1[1], ~in_1[2]);  // AND_Gate
  and and_2 (and_2_out, in_1[0], in_1[1], ~in_1[2]);  // AND_Gate
  and and_3 (and_3_out, in_1[0], ~in_1[1], in_1[2]);  // AND_Gate
  and and_4 (and_4_out, ~in_1[9], ~in_1[10], ~in_1[11], ~in_1[12]);  // AND_Gate
  and and_5 (and_5_out, ~in_1[0], ~in_1[1], ~in_1[2]);  // AND_Gate
  icodec icodec_1 (
    .icodein(in_1[12:9]), .unary(icodec_1_unary), .binary(icodec_1_binary), .memInstr(icodec_1_meminstr),
    .sw(icodec_1_sw), .li(icodec_1_li), .jreg(icodec_1_jreg), .j(icodec_1_j), .brnz(icodec_1_brnz));
  or or_1 (or_1_out, and_1_out, and_2_out, and_3_out);
  assign bit_extender_1_out = {{1{1'b1}}, in_1[2:0]};  // Bit_Extender bit_extender_1
  and and_6 (and_6_out, and_5_out, and_4_out);
  and and_7 (and_7_out, in_1[9], ~in_1[10], ~in_1[11], in_1[12]);  // AND_Gate
  and and_8 (and_8_out, ~in_1[9], in_1[10], in_1[11], in_1[12]);  // AND_Gate
  and and_9 (and_9_out, in_1[9], in_1[10], in_1[11], in_1[12], in_1[0]);
  and and_10 (and_10_out, ~in_1[9], in_1[10], ~in_1[11], in_1[12]);  // AND_Gate
  and and_11 (and_11_out, in_1[9], ~in_1[10], in_1[11], in_1[12]);  // AND_Gate
  and and_12 (and_12_out, in_1[9], in_1[10], ~in_1[11], in_1[12]);  // AND_Gate
  and and_13 (and_13_out, ~in_1[9], ~in_1[10], in_1[11], in_1[12]);  // AND_Gate
  and and_14 (and_14_out, icodec_1_meminstr, ~icodec_1_sw);  // AND_Gate
  Multiplexer #(.width(4), .disabled(0), .enable("false")) multiplexer_1 (
    .in0(in_1[12:9]), .in1(bit_extender_1_out), .out(multiplexer_1_out), .sel(and_4_out));
  and and_15 (and_15_out, icodec_1_j, in_1[0]);
  or or_2 (or_2_out, icodec_1_jreg, icodec_1_li);
  or or_3 (or_3_out, and_14_out, icodec_1_binary, icodec_1_unary);
  and and_16 (and_16_out, ~in_1[6], ~in_1[7], ~in_1[8]);  // AND_Gate
  Multiplexer #(.width(4), .enable("false")) multiplexer_2 (
    .in0(multiplexer_1_out), .in1(4'b0000), .out(multiplexer_2_out), .sel(and_6_out));
  or or_4 (or_4_out, and_7_out, and_8_out, and_9_out, and_10_out);
  Multiplexer #(.width(3), .enable("false")) multiplexer_3 (
    .in0(in_1[5:3]), .in1(in_1[8:6]), .out(multiplexer_3_out), .sel(or_2_out));
  assign bit_extender_2_out = {{9{1'b0}}, in_1[2:0]};  // Bit_Extender bit_extender_2
  assign bit_extender_3_out = {{6{1'b0}}, in_1[5:0]};  // Bit_Extender bit_extender_3
  assign bit_extender_4_out = {{6{in_1[5]}}, in_1[5:0]};  // Bit_Extender bit_extender_4
  assign addr = {{4{1'b0}}, in_1[8:1]};  // Bit_Extender bit_extender_5
  _3_12_bit_twos_complement_cla u_3_12_bit_twos_complement_cla_1 (
    .aIn(ins), .bIn(12'h1), .carryIn(1'b0), .Sum(n3_12_bit_twos_complement_cla_1_sum));  // open: Overflow
  and and_17 (except, or_3_out, and_16_out);
  Multiplexer #(.width(4), .enable("false")) multiplexer_4 (
    .in0(multiplexer_2_out), .in1(4'b0011), .out(multiplexer_4_out), .sel(or_4_out));
  or or_5 (or_5_out, and_15_out, icodec_1_brnz, and_18_out);
  Multiplexer #(.width(3), .enable("false")) multiplexer_5 (
    .in0(multiplexer_3_out), .in1(3'b000), .out(rs), .sel(or_5_out));
  Multiplexer #(.width(4), .enable("false")) multiplexer_6 (
    .in0(multiplexer_4_out), .in1(4'b1000), .out(multiplexer_6_out), .sel(and_11_out));
  Multiplexer #(.width(3), .enable("false")) multiplexer_7 (.in0(in_1[8:6]), .in1(3'b111), .out(rd), .sel(and_15_out));
  or or_6 (or_6_out, icodec_1_brnz, icodec_1_sw);
  Multiplexer #(.width(3), .enable("false")) multiplexer_8 (
    .in0(in_1[2:0]), .in1(in_1[8:6]), .out(multiplexer_8_out), .sel(or_6_out));
  and and_18 (and_18_out, or_1_out, icodec_1_unary);
  or or_7 (or_7_out, icodec_1_jreg, icodec_1_brnz);
  Multiplexer #(.width(12), .enable("false")) multiplexer_9 (
    .in0(bit_extender_2_out), .in1(bit_extender_3_out), .out(multiplexer_9_out), .sel(icodec_1_li));
  Multiplexer #(.width(12), .enable("false")) multiplexer_10 (
    .in0(multiplexer_9_out), .in1(bit_extender_4_out), .out(multiplexer_10_out), .sel(or_7_out));
  Multiplexer #(.width(4), .enable("false")) multiplexer_11 (
    .in0(multiplexer_6_out), .in1(4'b0001), .out(multiplexer_11_out), .sel(and_12_out));
  Multiplexer #(.width(4), .enable("false")) multiplexer_12 (
    .in0(multiplexer_11_out), .in1(4'b1011), .out(ALUopout), .sel(and_13_out));
  Multiplexer #(.width(3), .enable("false")) multiplexer_13 (
    .in0(multiplexer_8_out), .in1(in_1[5:3]), .out(rt), .sel(and_18_out));
  Multiplexer #(.width(12), .enable("false")) multiplexer_14 (
    .in0(multiplexer_10_out), .in1(addr), .out(multiplexer_14_out), .sel(icodec_1_j));
  Multiplexer #(.width(12), .enable("false")) multiplexer_15 (
    .in0(multiplexer_14_out), .in1(n3_12_bit_twos_complement_cla_1_sum), .out(imm), .sel(and_15_out));

  assign icode = in_1[12:9];

  // Other names for the same wires on the sheet: t0[3:0] = in_1[12:9]; t1[2:0] = rd; t2[2:0] = rs; t3[2:0] = rt;
  //   t4[11:0] = imm; t5[11:0] = addr; t6[3:0] = ALUopout; t7 = except

  // Notes on the sheet:
  //   ic
  //   pc
  //   rs
  //   rd
  //   im
  //   rt
  //   ad
endmodule

module control (
  input  [3:0] a,
  output MemRead,
  output MemWrite,
  output MemToReg,
  output RegWrite,
  output ALUsrc,
  output jumpReg,
  output babs,
  output loadUpperImm,
  output brNeqZero
);

  wire and_4_out, and_5_out, and_6_out, and_7_out, and_8_out, and_9_out, and_10_out, and_12_out, and_13_out,
       not_1_out, not_2_out, not_3_out, not_4_out, not_5_out, not_6_out, not_7_out, not_8_out, not_9_out,
       not_10_out, not_11_out, not_12_out, not_13_out, not_14_out, not_15_out, not_16_out, not_17_out,
       not_18_out;

  not not_1 (not_1_out, a[2]);
  not not_2 (not_2_out, a[1]);
  not not_3 (not_3_out, a[2]);
  not not_4 (not_4_out, a[0]);
  not not_5 (not_5_out, a[2]);
  not not_6 (not_6_out, a[1]);
  not not_7 (not_7_out, a[2]);
  not not_8 (not_8_out, a[1]);
  not not_9 (not_9_out, a[1]);
  not not_10 (not_10_out, a[0]);
  not not_11 (not_11_out, a[2]);
  not not_12 (not_12_out, a[2]);
  not not_13 (not_13_out, a[0]);
  not not_14 (not_14_out, a[1]);
  not not_15 (not_15_out, a[0]);
  not not_16 (not_16_out, a[1]);
  and and_1 (MemRead, a[3], not_1_out, not_2_out, a[0]);
  and and_2 (MemWrite, a[3], not_3_out, a[1], not_4_out);
  and and_3 (MemToReg, a[3], not_5_out, not_6_out, a[0]);
  not not_17 (not_17_out, a[3]);
  and and_4 (and_4_out, not_7_out, not_8_out);
  and and_5 (and_5_out, not_9_out, not_10_out);
  and and_6 (and_6_out, a[1], a[0]);
  and and_7 (and_7_out, a[3], not_11_out, a[0]);
  and and_8 (and_8_out, a[3], not_12_out, a[1]);
  and and_9 (and_9_out, a[3], a[2], not_13_out);
  and and_10 (and_10_out, a[3], a[2], a[1], a[0]);
  and and_11 (jumpReg, a[3], a[2], a[1], not_18_out);
  not not_18 (not_18_out, a[0]);
  and and_12 (and_12_out, a[3], a[2], a[0]);
  and and_13 (and_13_out, a[3], a[2], a[1]);
  and and_14 (loadUpperImm, a[3], a[2], not_14_out, not_15_out);
  and and_15 (brNeqZero, a[3], a[2], not_16_out, a[0]);
  or or_1 (RegWrite, not_17_out, and_4_out, and_5_out, and_6_out);
  or or_2 (ALUsrc, and_7_out, and_8_out, and_9_out, and_10_out);
  or or_3 (babs, and_12_out, and_13_out);
endmodule

module icodec (
  input  [3:0] icodein,
  output unary,
  output binary,
  output memInstr,
  output sw,
  output li,
  output jreg,
  output j,
  output brnz
);

  wire and_2_out, and_3_out, and_4_out, and_5_out, and_6_out, and_8_out, and_9_out, not_1_out, not_2_out,
       not_3_out, not_4_out;

  not not_1 (not_1_out, icodein[2]);
  not not_2 (not_2_out, icodein[3]);
  not not_3 (not_3_out, icodein[0]);
  not not_4 (not_4_out, icodein[1]);
  and and_1 (unary, not_3_out, not_4_out, not_1_out, not_2_out);
  and and_2 (and_2_out, not_2_out, icodein[0]);
  and and_3 (and_3_out, not_2_out, icodein[1]);
  and and_4 (and_4_out, not_2_out, icodein[2]);
  and and_5 (and_5_out, icodein[3], not_1_out, not_4_out, not_3_out);
  and and_6 (and_6_out, icodein[3], not_1_out, not_4_out, icodein[0]);
  and and_7 (sw, icodein[3], not_1_out, icodein[1], not_3_out);
  and and_8 (and_8_out, icodein[3], not_1_out, icodein[1], icodein[0]);
  and and_9 (and_9_out, icodein[3], icodein[2], not_4_out, not_3_out);
  and and_10 (jreg, icodein[3], icodein[2], icodein[1], not_3_out);
  and and_11 (j, icodein[3], icodein[2], icodein[1], icodein[0]);
  and and_12 (brnz, icodein[3], icodein[2], not_4_out, icodein[0]);
  or or_1 (binary, and_2_out, and_3_out, and_4_out, and_5_out);
  or or_2 (memInstr, and_6_out, sw);
  or or_3 (li, and_8_out, and_9_out);

  // Other names for the same wires on the sheet: t1 = unary; t2 = binary; t3 = memInstr; t4 = sw; t5 = li; t6 = jreg;
  //   t7 = j; t8 = brnz
endmodule

module exception_handler (
  input  [12:0] \input 
);
endmodule
