// Logisim project project_memory.circ as structural Verilog
module _1_12_bit_register (
  input  c,
  input  [11:0] D,
  input  write,
  input  reset,
  output [11:0] Q
);

  D_Flip_Flop #(.trigger("falling")) d_ff_1 (
    .clk(c), .D(D[0]), .Q(Q[0]), .en(write), .reset(reset));  // open: Qn, preset
  D_Flip_Flop #(.trigger("falling")) d_ff_2 (
    .clk(c), .D(D[1]), .Q(Q[1]), .en(write), .reset(reset));  // open: Qn, preset
  D_Flip_Flop #(.trigger("falling")) d_ff_3 (
    .clk(c), .D(D[2]), .Q(Q[2]), .en(write), .reset(reset));  // open: Qn, preset
  D_Flip_Flop #(.trigger("falling")) d_ff_4 (
    .clk(c), .D(D[3]), .Q(Q[3]), .en(write), .reset(reset));  // open: Qn, preset
  D_Flip_Flop #(.trigger("falling")) d_ff_5 (
    .clk(c), .D(D[4]), .Q(Q[4]), .en(write), .reset(reset));  // open: Qn, preset
  D_Flip_Flop #(.trigger("falling")) d_ff_6 (
    .clk(c), .D(D[5]), .Q(Q[5]), .en(write), .reset(reset));  // open: Qn, preset
  D_Flip_Flop #(.trigger("falling")) d_ff_7 (
    .clk(c), .D(D[6]), .Q(Q[6]), .en(write), .reset(reset));  // open: Qn, preset
  D_Flip_Flop #(.trigger("falling")) d_ff_8 (
    .clk(c), .D(D[7]), .Q(Q[7]), .en(write), .reset(reset));  // open: Qn, preset
  D_Flip_Flop #(.trigger("falling")) d_ff_9 (
    .clk(c), .D(D[8]), .Q(Q[8]), .en(write), .reset(reset));  // open: Qn, preset
  D_Flip_Flop #(.trigger("falling")) d_ff_10 (
    .clk(c), .D(D[9]), .Q(Q[9]), .en(write), .reset(reset));  // open: Qn, preset
  D_Flip_Flop #(.trigger("falling")) d_ff_11 (
    .clk(c), .D(D[10]), .Q(Q[10]), .en(write), .reset(reset));  // open: Qn, preset
  D_Flip_Flop #(.trigger("falling")) d_ff_12 (
    .clk(c), .D(D[11]), .Q(Q[11]), .en(write), .reset(reset));  // open: Qn, preset
endmodule

module _2_register_file (
  input  [11:0] \input ,
  input  [2:0] rd,
  input  clock,
  input  write,
  input  clear,
  input  [2:0] rs,
  input  [2:0] rt,
  output [11:0] _0,
  output [11:0] _1,
  output [11:0] _2,
  output [11:0] _3,
  output [11:0] _4,
  output [11:0] _5,
  output [11:0] _6,
  output [11:0] _7,
  output [11:0] rsOut,
  output [11:0] rtOut
);

  wire and_1_out, and_2_out, and_3_out, and_4_out, and_5_out, and_6_out, and_7_out, and_8_out,
       n2_decoder_1_i0, n2_decoder_1_i1, n2_decoder_1_i2, n2_decoder_1_i3, n2_decoder_1_i4, n2_decoder_1_i5,
       n2_decoder_1_i6, n2_decoder_1_i7;

  _2_decoder u_2_decoder_1 (
    .in(rd), .i0(n2_decoder_1_i0), .i1(n2_decoder_1_i1), .i2(n2_decoder_1_i2), .i3(n2_decoder_1_i3),
    .i4(n2_decoder_1_i4), .i5(n2_decoder_1_i5), .i6(n2_decoder_1_i6), .i7(n2_decoder_1_i7));
  and and_1 (and_1_out, clock, n2_decoder_1_i0);
  and and_2 (and_2_out, clock, n2_decoder_1_i1);
  and and_3 (and_3_out, clock, n2_decoder_1_i2);
  and and_4 (and_4_out, clock, n2_decoder_1_i3);
  and and_5 (and_5_out, clock, n2_decoder_1_i4);
  and and_6 (and_6_out, clock, n2_decoder_1_i5);
  and and_7 (and_7_out, clock, n2_decoder_1_i6);
  and and_8 (and_8_out, clock, n2_decoder_1_i7);
  _1_12_bit_register u_1_12_bit_register_1 (.c(and_1_out), .D({12{1'b0}}), .write(write), .reset(clear), .Q(_0));
  _1_12_bit_register u_1_12_bit_register_2 (.c(and_2_out), .D(\input ), .write(write), .reset(clear), .Q(_1));
  _1_12_bit_register u_1_12_bit_register_3 (.c(and_3_out), .D(\input ), .write(write), .reset(clear), .Q(_2));
  _1_12_bit_register u_1_12_bit_register_4 (.c(and_4_out), .D(\input ), .write(write), .reset(clear), .Q(_3));
  _1_12_bit_register u_1_12_bit_register_5 (.c(and_5_out), .D(\input ), .write(write), .reset(clear), .Q(_4));
  _1_12_bit_register u_1_12_bit_register_6 (.c(and_6_out), .D(\input ), .write(write), .reset(clear), .Q(_5));
  _1_12_bit_register u_1_12_bit_register_7 (.c(and_7_out), .D(\input ), .write(write), .reset(clear), .Q(_6));
  _1_12_bit_register u_1_12_bit_register_8 (.c(and_8_out), .D(\input ), .write(write), .reset(clear), .Q(_7));
  Multiplexer #(.select(3), .width(12)) multiplexer_1 (
    .in0(_0), .in1(_1), .in2(_2), .in3(_3), .in4(_4), .in5(_5), .in6(_6), .in7(_7), .out(rsOut), .sel(rs));  // open: en
  Multiplexer #(.select(3), .width(12)) multiplexer_2 (
    .in0(_0), .in1(_1), .in2(_2), .in3(_3), .in4(_4), .in5(_5), .in6(_6), .in7(_7), .out(rtOut), .sel(rt));  // open: en
endmodule

module _2_decoder (
  input  [2:0] in,
  output i0,
  output i1,
  output i2,
  output i3,
  output i4,
  output i5,
  output i6,
  output i7
);

  wire not_1_out, not_2_out, not_3_out, not_4_out, not_5_out, not_6_out, not_7_out, not_8_out, not_9_out,
       not_10_out, not_11_out, not_12_out;

  not not_1 (not_1_out, in[2]);
  not not_2 (not_2_out, in[1]);
  not not_3 (not_3_out, in[0]);
  not not_4 (not_4_out, in[2]);
  not not_5 (not_5_out, in[1]);
  not not_6 (not_6_out, in[2]);
  not not_7 (not_7_out, in[0]);
  not not_8 (not_8_out, in[2]);
  not not_9 (not_9_out, in[1]);
  not not_10 (not_10_out, in[0]);
  not not_11 (not_11_out, in[1]);
  not not_12 (not_12_out, in[0]);
  and and_1 (i7, in[2], in[1], in[0]);
  and and_2 (i0, not_1_out, not_2_out, not_3_out);
  and and_3 (i1, not_4_out, not_5_out, in[0]);
  and and_4 (i2, not_6_out, in[1], not_7_out);
  and and_5 (i3, not_8_out, in[1], in[0]);
  and and_6 (i4, in[2], not_9_out, not_10_out);
  and and_7 (i5, in[2], not_11_out, in[0]);
  and and_8 (i6, in[2], in[1], not_12_out);
endmodule

module _3_counter (
  input  C,
  input  [11:0] D,
  output [11:0] O
);

  wire comparator_1_lt;
  wire [11:0] multiplexer_1_out, n3_12_bit_twos_complement_cla_1_sum;

  Comparator #(.width(12)) comparator_1 (
    .a(n3_12_bit_twos_complement_cla_1_sum), .b(D), .lt(comparator_1_lt));  // open: gt, eq
  Multiplexer #(.width(12)) multiplexer_1 (
    .in0({12{1'b0}}), .in1(n3_12_bit_twos_complement_cla_1_sum), .out(multiplexer_1_out),
    .sel(comparator_1_lt));  // open: en
  _3_12_bit_twos_complement_cla u_3_12_bit_twos_complement_cla_1 (
    .aIn(O), .bIn(12'h1), .carryIn(1'b0), .Sum(n3_12_bit_twos_complement_cla_1_sum));  // open: Overflow
  _1_12_bit_register u_1_12_bit_register_1 (.c(C), .D(multiplexer_1_out), .write(1'b1), .reset(1'b0), .Q(O));
endmodule

module _4_finite_state_traffic (
  output [11:0] out_1
);

  wire clock_1_out, decoder_1_out1, decoder_1_out2, decoder_1_out3, decoder_2_out1, decoder_2_out2,
       decoder_2_out3;
  wire [1:0] bitselector_1_out, bitselector_2_out;
  wire [11:0] n1_12_bit_register_1_q, n1_12_bit_register_2_q, n4_dec_1_1_out_2, n4_dec_2_1_out_2;

  Clock clock_1 (.out(clock_1_out));
  _3_counter u_3_counter_1 (.C(clock_1_out), .D(12'h1c), .O(out_1));
  _4_dec_1 u_4_dec_1_1 (.in_1(out_1), .out_2(n4_dec_1_1_out_2));
  _4_dec_2 u_4_dec_2_1 (.in_1(out_1), .out_2(n4_dec_2_1_out_2));
  _1_12_bit_register u_1_12_bit_register_1 (
    .c(clock_1_out), .D(n4_dec_1_1_out_2), .Q(n1_12_bit_register_1_q));  // open: write, reset
  _1_12_bit_register u_1_12_bit_register_2 (
    .c(clock_1_out), .D(n4_dec_2_1_out_2), .Q(n1_12_bit_register_2_q));  // open: write, reset
  BitSelector #(.width(12), .group(2)) bitselector_1 (
    .in(n1_12_bit_register_1_q), .out(bitselector_1_out), .sel(3'b000));
  Decoder #(.select(2)) decoder_1 (
    .out1(decoder_1_out1), .out2(decoder_1_out2), .out3(decoder_1_out3), .sel(bitselector_1_out));  // open: out0, en
  BitSelector #(.width(12), .group(2)) bitselector_2 (
    .in(n1_12_bit_register_2_q), .out(bitselector_2_out), .sel(3'b000));
  Decoder #(.select(2)) decoder_2 (
    .out1(decoder_2_out1), .out2(decoder_2_out2), .out3(decoder_2_out3), .sel(bitselector_2_out));  // open: out0, en
  LED led_1 (.in(clock_1_out));
  LED led_2 (.in(decoder_1_out3));
  LED led_3 (.in(decoder_1_out2));
  LED led_4 (.in(decoder_1_out1));
  LED led_5 (.in(decoder_2_out3));
  LED led_6 (.in(decoder_2_out2));
  LED led_7 (.in(decoder_2_out1));
endmodule

// 1
module _4_dec_1 (
  input  [11:0] in_1,
  output [11:0] out_2
);

  wire and_1_out, and_2_out, and_3_out, not_1_out, not_2_out, not_3_out, not_4_out, or_1_out;
  wire [1:0] multiplexer_1_out, multiplexer_2_out, multiplexer_3_out, or_2_out;

  and and_1 (and_1_out, in_1[3], in_1[2]);
  not not_1 (not_1_out, in_1[4]);
  not not_2 (not_2_out, in_1[2]);
  not not_3 (not_3_out, in_1[4]);
  not not_4 (not_4_out, in_1[3]);
  or or_1 (or_1_out, and_1_out, in_1[4]);
  and and_2 (and_2_out, not_1_out, in_1[3], not_2_out);
  and and_3 (and_3_out, not_3_out, not_4_out);
  Multiplexer #(.width(2)) multiplexer_1 (
    .in0(2'b00), .in1(2'b11), .out(multiplexer_1_out), .sel(or_1_out));  // open: en
  Multiplexer #(.width(2)) multiplexer_2 (
    .in0(2'b00), .in1(2'b10), .out(multiplexer_2_out), .sel(and_2_out));  // open: en
  Multiplexer #(.width(2)) multiplexer_3 (
    .in0(2'b00), .in1(2'b01), .out(multiplexer_3_out), .sel(and_3_out));  // open: en
  assign or_2_out = multiplexer_1_out | multiplexer_2_out | multiplexer_3_out;  // OR_Gate or_2, 2 bits wide
  assign out_2 = {{10{1'b0}}, or_2_out};  // Bit_Extender bit_extender_1
endmodule

// 2
module _4_dec_2 (
  input  [11:0] in_1,
  output [11:0] out_2
);

  wire and_1_out, and_2_out, and_3_out, and_4_out, and_5_out, and_6_out, and_7_out, and_8_out, and_9_out,
       not_1_out, not_2_out, not_3_out, not_4_out, not_5_out, not_6_out, not_7_out, not_8_out, not_9_out,
       not_10_out, not_11_out, not_12_out, not_13_out, or_1_out, or_2_out, or_3_out;
  wire [1:0] multiplexer_1_out, multiplexer_2_out, multiplexer_3_out, or_4_out;

  not not_1 (not_1_out, in_1[4]);
  not not_2 (not_2_out, in_1[3]);
  not not_3 (not_3_out, in_1[4]);
  not not_4 (not_4_out, in_1[2]);
  not not_5 (not_5_out, in_1[1]);
  not not_6 (not_6_out, in_1[3]);
  not not_7 (not_7_out, in_1[2]);
  not not_8 (not_8_out, in_1[1]);
  not not_9 (not_9_out, in_1[4]);
  not not_10 (not_10_out, in_1[3]);
  not not_11 (not_11_out, in_1[2]);
  not not_12 (not_12_out, in_1[3]);
  not not_13 (not_13_out, in_1[1]);
  and and_1 (and_1_out, not_1_out, not_2_out);
  and and_2 (and_2_out, not_3_out, not_4_out);
  and and_3 (and_3_out, in_1[3], in_1[2], not_5_out);
  and and_4 (and_4_out, in_1[4], in_1[3], in_1[1]);
  and and_5 (and_5_out, in_1[4], not_6_out, in_1[2], in_1[1]);
  and and_6 (and_6_out, in_1[4], in_1[3], not_7_out, not_8_out);
  and and_7 (and_7_out, not_9_out, in_1[3], in_1[2], in_1[1]);
  and and_8 (and_8_out, in_1[4], not_10_out, not_11_out);
  and and_9 (and_9_out, in_1[4], not_12_out, not_13_out);
  or or_1 (or_1_out, and_1_out, and_2_out, and_3_out, and_4_out);
  or or_2 (or_2_out, and_5_out, and_6_out);
  or or_3 (or_3_out, and_7_out, and_8_out, and_9_out);
  Multiplexer #(.width(2)) multiplexer_1 (
    .in0(2'b00), .in1(2'b11), .out(multiplexer_1_out), .sel(or_1_out));  // open: en
  Multiplexer #(.width(2)) multiplexer_2 (
    .in0(2'b00), .in1(2'b10), .out(multiplexer_2_out), .sel(or_2_out));  // open: en
  Multiplexer #(.width(2)) multiplexer_3 (
    .in0(2'b00), .in1(2'b01), .out(multiplexer_3_out), .sel(or_3_out));  // open: en
  assign or_4_out = multiplexer_1_out | multiplexer_2_out | multiplexer_3_out;  // OR_Gate or_4, 2 bits wide
  assign out_2 = {{10{1'b0}}, or_4_out};  // Bit_Extender bit_extender_1
endmodule

module _6_stack (
  input  [11:0] in_1,
  input  push,
  input  clear,
  input  pop,
  output [11:0] peek,
  output E
);

  wire and_1_out, and_2_out, clock_1_out, comparator_1_eq, or_1_out, or_2_out;
  wire [11:0] minus_1_sum, multiplexer_1_out, multiplexer_2_out, n6_counter_v2_1_o, not_1_out;

  Clock clock_1 (.out(clock_1_out));
  Multiplexer #(.width(12)) multiplexer_1 (
    .in0({12{1'b1}}), .in1({12{1'b0}}), .out(multiplexer_1_out), .sel(clear));  // open: en
  or or_1 (or_1_out, clear, or_2_out);
  or or_2 (or_2_out, push, and_1_out);
  and and_1 (and_1_out, pop, ~comparator_1_eq);  // AND_Gate
  _6_counter_v2 u_6_counter_v2_1 (.C(or_1_out), .D(multiplexer_1_out), .sub(and_1_out), .O(n6_counter_v2_1_o));
  _3_12_bit_twos_complement_cla minus_1 (
    .aIn(n6_counter_v2_1_o), .bIn(not_1_out), .carryIn(1'b1), .Sum(minus_1_sum));  // open: Overflow
  assign not_1_out = ~12'h1;  // NOT_Gate not_1, 12 bits wide
  and and_2 (and_2_out, ~push, ~pop, ~clear);  // AND_Gate
  Multiplexer #(.width(12)) multiplexer_2 (
    .in0(n6_counter_v2_1_o), .in1(minus_1_sum), .out(multiplexer_2_out), .sel(and_2_out));  // open: en
  Comparator #(.width(12)) comparator_1 (.a(n6_counter_v2_1_o), .b({12{1'b0}}), .eq(comparator_1_eq));  // open: gt, lt
  and and_3 (E, comparator_1_eq, pop);
  RAM #(.addrWidth(12), .dataWidth(12), .bus("separate")) ram_1 (
    .addr(multiplexer_2_out), .din(in_1), .data(peek), .str(push), .clk(clock_1_out), .ld(and_2_out),
    .clr(clear));  // open: sel
endmodule

// cnt
module _6_counter_v2 (
  input  C,
  input  [11:0] D,
  input  sub,
  output [11:0] O
);

  wire comparator_1_lt;
  wire [11:0] multiplexer_1_out, multiplexer_2_out, n3_12_bit_twos_complement_cla_1_sum, not_1_out;

  Comparator #(.width(12), .mode("unsigned")) comparator_1 (
    .a(n3_12_bit_twos_complement_cla_1_sum), .b(D), .lt(comparator_1_lt));  // open: gt, eq
  Multiplexer #(.width(12)) multiplexer_1 (
    .in0({12{1'b0}}), .in1(n3_12_bit_twos_complement_cla_1_sum), .out(multiplexer_1_out),
    .sel(comparator_1_lt));  // open: en
  _3_12_bit_twos_complement_cla u_3_12_bit_twos_complement_cla_1 (
    .aIn(O), .bIn(multiplexer_2_out), .carryIn(sub), .Sum(n3_12_bit_twos_complement_cla_1_sum));  // open: Overflow
  _1_12_bit_register u_1_12_bit_register_1 (.c(C), .D(multiplexer_1_out), .write(1'b1), .reset(1'b0), .Q(O));
  Multiplexer #(.width(12)) multiplexer_2 (
    .in0(12'h1), .in1(not_1_out), .out(multiplexer_2_out), .sel(sub));  // open: en
  assign not_1_out = ~12'h1;  // NOT_Gate not_1, 12 bits wide
endmodule
